# Fritzing sketch ST_IKBD_RTC (saved by Fritzing 0.9.3b)

parts:
  ZS-042_RTC1 = ZS-042 RTC Module
  Part1 = Arduino Pro Mini (5V)
  J1 = female pin header, 8 pins [form="♀ (female)"]
  J2 = male pin header, 8 pins [form="♂ (male)"]

nets:
  GND: ZS-042_RTC1.GND, Part1.GND, J1.pin1, J2.pin1
  N1: ZS-042_RTC1.VCC, Part1.A3
  N2: ZS-042_RTC1.SDA, Part1.A4
  N3: ZS-042_RTC1.SCL, Part1.A5
  N4: Part1.VCC, J1.pin4, J2.pin4
  N5: Part1.D2, J1.pin6, J2.pin6
  N6: Part1.RXI, J2.pin5
  N7: Part1.TXO, J1.pin5
  N8: J1.pin3, J2.pin3
  N9: J1.pin7, J2.pin7
  N10: J1.pin8, J2.pin8

notes:
  ST
  KB
